# Fritzing sketch Circuit Schematic (saved by Fritzing 0.9.3b)
breadboards: 1

parts:
  U1 = ESP8266 NodeMCU LoLin base
  U2 = 4-Channel 5v Relay Shield [package=relay-4ch5v10a]
  PSU1 = Adjustable Breadboard Power Supply  # not connected
  BULB1 = Incandescent light bulb small [package="bulb sm"]
  BULB2 = Incandescent light bulb small [package="bulb sm"]
  PIR1 = PIR sensor
  JACK1 = 2.1mm Barrel Jack with Terminal Block
  JACK2 = 2.1mm Barrel Jack with Terminal Block

nets:
  GND: U1.GND1-3, U1.GND3-0, U1.GND3-2, U1.GND8-10, U2.GND, PIR1.GND
  VCC: U1.3V1-0, U1.3V1-2, U1.3V3-0, U2.VCC, U2.IN4, PIR1.VDD
  N1: U1.D5-0, U2.IN1
  N2: U1.D6-0, U2.IN2
  N3: U1.D8-0, U1.D8-3, PIR1.SIG
  N4: U2.K1-Off, JACK1.POS
  N5: U2.K1-On, BULB2.1
  N6: U2.K2-Off, JACK2.POS
  N7: U2.K2-On, BULB1.1
  N8: BULB1.2, JACK2.NEG
  N9: BULB2.2, JACK1.NEG

notes:
  240V

custom parts:
  ESP8266 NodeMCU LoLin base: ESP8266 based NodeMCU Base
  4-Channel 5v Relay Shield: 4 Channel 5v Relay Shield w. 2x SPD-06VDC-SD-C
